# Fritzing sketch fireplace (saved by Fritzing 0.9.3b)
breadboards: 1

parts:
  Part1 = Arduino Nano (Rev3.0)
  R3 = Resistor Mini [tolerance=±5% resistance=220 package=THT]
  LED2 = LED - 3mm [color="Red (633nm)" package="3 mm [THT]"]
  LED3 = LED - 3mm [color="Yellow (595nm)" package="3 mm [THT]"]
  R5 = Resistor Mini [tolerance=±5% resistance=220 package=THT]
  R6 = Resistor Mini [tolerance=±5% resistance=220 package=THT]
  R7 = Resistor Mini [tolerance=±5% resistance=220 package=THT]
  R8 = Resistor Mini [tolerance=±5% resistance=220 package=THT]
  R9 = Resistor Mini [tolerance=±5% resistance=220 package=THT]
  LED4 = LED - 3mm [color="Red (633nm)" package="3 mm [THT]"]
  LED5 = LED - 3mm [color="Yellow (595nm)" package="3 mm [THT]"]
  LED6 = LED - 3mm [color="Red (633nm)" package="3 mm [THT]"]
  LED7 = LED - 3mm [color="Red (633nm)" package="3 mm [THT]"]
  J1 = Piezo Speaker

nets:
  N1: Part1.GND, R3.Pin_1, R5.Pin_1, R6.Pin_1, R7.Pin_1, R8.Pin_1, R9.Pin_1, J1.pin1
  N2: Part1.D3, LED4.anode
  N3: Part1.D4, LED7.anode
  N4: Part1.D6, LED3.anode
  N5: Part1.D7, LED5.anode
  N6: Part1.D9, LED6.anode
  N7: Part1.D10, LED2.anode
  N8: Part1.A3, J1.pin2
  N9: R3.Pin_0, LED2.cathode
  N10: LED3.cathode, R5.Pin_0
  N11: R6.Pin_0, LED4.cathode
  N12: R7.Pin_0, LED6.cathode
  N13: R8.Pin_0, LED5.cathode
  N14: R9.Pin_0, LED7.cathode

custom parts:
  Resistor Mini: A generic resistor (0.25W)
