# Fritzing sketch simon-says (saved by Fritzing 0.9.3b)
breadboards: 1

parts:
  Part1 = Arduino Nano (Rev3.0)
  S1 = Reed switch [package=THT]
  S2 = Pushbutton [package="[THT]"]
  S3 = Pushbutton [package="[THT]"]
  LED1 = LED - 3mm [color="Blue (430nm)" package="3 mm [THT]"]
  R2 = Resistor Mini [tolerance=±5% resistance=220 package=THT]
  R3 = Resistor Mini [tolerance=±5% resistance=220 package=THT]
  LED2 = LED - 3mm [color="Red (633nm)" package="3 mm [THT]"]
  R4 = Resistor Mini [tolerance=±5% resistance=220 package=THT]
  LED3 = LED - 3mm [color="Yellow (595nm)" package="3 mm [THT]"]

nets:
  N1: Part1.GND, S1.pin_2, S2.Pin_3, S2.Pin_4, S3.Pin_1, S3.Pin_2, LED1.cathode, LED2.cathode, LED3.cathode
  N2: Part1.D3, R2.Pin_0
  N3: Part1.D5, R3.Pin_0
  N4: Part1.D8, R4.Pin_0
  N5: Part1.A7, S1.pin_1
  N6: Part1.A6, S2.Pin_1, S2.Pin_2
  N7: Part1.A5, S3.Pin_3, S3.Pin_4
  N8: LED1.anode, R2.Pin_1
  N9: R3.Pin_1, LED2.anode
  N10: R4.Pin_1, LED3.anode

custom parts:
  Resistor Mini: A generic resistor (0.25W)
